// Logisim project ALU-Circuits.circ as structural Verilog: 9 circuits, main circuit ALU8
module Tutorial (
  input  [7:0] X,
  output O2,
  output [7:0] O1
);

  nand nand_1 (O1[0], X[0], X[7]);

  assign O1[7:1] = X[7:1];
  assign O2 = O1[0];
endmodule

module twosComplement (
  input  [7:0] X,
  output [7:0] COMPL
);

  wire [7:0] not_1_out;

  assign not_1_out = ~X;  // NOT_Gate not_1, 8 bits wide
  FULLADDER8 fulladder8_1 (.Y(8'h1), .X(not_1_out), .SUM(COMPL));  // open: CIN, COUT
endmodule

module eightBitShifter (
  input  [7:0] Number,
  input  Direction,
  output [7:0] out_3
);

  wire and_2_out, and_3_out, and_4_out, and_5_out, and_6_out, and_7_out, and_8_out, and_9_out, and_10_out,
       and_11_out, and_12_out, and_13_out, and_14_out, and_15_out, LeftT, not_1_out, RightT;

  not not_1 (not_1_out, Direction);
  and and_1 (LeftT, not_1_out, Number[7]);
  and and_2 (and_2_out, Number[7], Direction);
  or or_1 (out_3[7], RightT, and_3_out);
  and and_3 (and_3_out, not_1_out, Number[6]);
  and and_4 (and_4_out, Number[6], Direction);
  or or_2 (out_3[6], and_2_out, and_5_out);
  and and_5 (and_5_out, not_1_out, Number[5]);
  or or_3 (out_3[5], and_4_out, and_7_out);
  and and_6 (and_6_out, Number[5], Direction);
  and and_7 (and_7_out, not_1_out, Number[4]);
  and and_8 (and_8_out, Number[4], Direction);
  or or_4 (out_3[4], and_6_out, and_9_out);
  and and_9 (and_9_out, not_1_out, Number[3]);
  or or_5 (out_3[3], and_8_out, and_11_out);
  and and_10 (and_10_out, Number[3], Direction);
  and and_11 (and_11_out, not_1_out, Number[2]);
  and and_12 (and_12_out, Number[2], Direction);
  or or_6 (out_3[2], and_10_out, and_13_out);
  and and_13 (and_13_out, not_1_out, Number[1]);
  or or_7 (out_3[1], and_12_out, and_15_out);
  and and_14 (and_14_out, Number[1], Direction);
  and and_15 (and_15_out, not_1_out, Number[0]);
  and and_16 (RightT, Number[0], Direction);
  or or_8 (out_3[0], and_14_out, LeftT);
endmodule

module rotl (
  input  [7:0] X,
  input  [2:0] Y,
  output [7:0] out_3
);

  wire [7:0] Shift1, Shift2, Shift3, Shift4, Shift5, Shift6, Shift7, Shift8;

  Multiplexer #(.select(3), .width(8)) multiplexer_1 (
    .in0(Shift1), .in1(Shift2), .in2(Shift3), .in3(Shift4), .in4(Shift5), .in5(Shift6), .in6(Shift7),
    .in7(Shift8), .out(out_3), .sel(Y));
  eightBitShifter Shifter (.Number(X), .Direction(1'b0), .out_3(Shift1));
  eightBitShifter Shifter_4 (.Number(Shift4), .Direction(1'b0), .out_3(Shift5));
  eightBitShifter Shifter_1 (.Number(Shift1), .Direction(1'b0), .out_3(Shift2));
  eightBitShifter Shifter_5 (.Number(Shift5), .Direction(1'b0), .out_3(Shift6));
  eightBitShifter Shifter_2 (.Number(Shift2), .Direction(1'b0), .out_3(Shift3));
  eightBitShifter Shifter_6 (.Number(Shift6), .Direction(1'b0), .out_3(Shift7));
  eightBitShifter Shifter_3 (.Number(Shift3), .Direction(1'b0), .out_3(Shift4));
  eightBitShifter Shifter_7 (.Number(Shift7), .Direction(1'b0), .out_3(Shift8));
endmodule

module rotr (
  input  [7:0] X,
  input  [2:0] Y,
  output [7:0] ROUT
);

  wire [7:0] Shift1, Shift2, Shift3, Shift4, Shift5, Shift6, Shift7, Shift8;

  Multiplexer #(.select(3), .width(8)) multiplexer_1 (
    .in0(Shift1), .in1(Shift2), .in2(Shift3), .in3(Shift4), .in4(Shift5), .in5(Shift6), .in6(Shift7),
    .in7(Shift8), .out(ROUT), .sel(Y));
  eightBitShifter Shifter (.Number(X), .Direction(1'b1), .out_3(Shift1));
  eightBitShifter Shifter_4 (.Number(Shift4), .Direction(1'b1), .out_3(Shift5));
  eightBitShifter Shifter_1 (.Number(Shift1), .Direction(1'b1), .out_3(Shift2));
  eightBitShifter Shifter_5 (.Number(Shift5), .Direction(1'b1), .out_3(Shift6));
  eightBitShifter Shifter_2 (.Number(Shift2), .Direction(1'b1), .out_3(Shift3));
  eightBitShifter Shifter_6 (.Number(Shift6), .Direction(1'b1), .out_3(Shift7));
  eightBitShifter Shifter_3 (.Number(Shift3), .Direction(1'b1), .out_3(Shift4));
  eightBitShifter Shifter_7 (.Number(Shift7), .Direction(1'b1), .out_3(Shift8));
endmodule

module fullAdder (
  input  A,
  input  B,
  input  CarryIn,
  output SumOut,
  output CarryOut
);

  wire and_1_out, and_2_out, xor_1_out;

  and and_1 (and_1_out, A, B);
  xor xor_1 (xor_1_out, A, B);
  xor xor_2 (SumOut, xor_1_out, CarryIn);
  and and_2 (and_2_out, CarryIn, xor_1_out);
  or or_1 (CarryOut, and_2_out, and_1_out);
endmodule

module FULLADDER8 (
  input  [7:0] Y,
  input  [7:0] X,
  input  CIN,
  output COUT,
  output [7:0] SUM
);

  wire fulladder_2_carryout, fulladder_3_carryout, fulladder_4_carryout, fulladder_5_carryout,
       fulladder_6_carryout, fulladder_7_carryout, fulladder_8_carryout;

  fullAdder fulladder_1 (.CarryIn(fulladder_2_carryout), .A(X[7]), .B(Y[7]), .SumOut(SUM[7]), .CarryOut(COUT));
  fullAdder fulladder_2 (
    .CarryIn(fulladder_3_carryout), .A(X[6]), .B(Y[6]), .SumOut(SUM[6]), .CarryOut(fulladder_2_carryout));
  fullAdder fulladder_3 (
    .CarryIn(fulladder_4_carryout), .A(X[5]), .B(Y[5]), .SumOut(SUM[5]), .CarryOut(fulladder_3_carryout));
  fullAdder fulladder_4 (
    .CarryIn(fulladder_5_carryout), .A(X[4]), .B(Y[4]), .SumOut(SUM[4]), .CarryOut(fulladder_4_carryout));
  fullAdder fulladder_5 (
    .CarryIn(fulladder_6_carryout), .A(X[3]), .B(Y[3]), .SumOut(SUM[3]), .CarryOut(fulladder_5_carryout));
  fullAdder fulladder_6 (
    .CarryIn(fulladder_7_carryout), .A(X[2]), .B(Y[2]), .SumOut(SUM[2]), .CarryOut(fulladder_6_carryout));
  fullAdder fulladder_7 (
    .CarryIn(fulladder_8_carryout), .A(X[1]), .B(Y[1]), .SumOut(SUM[1]), .CarryOut(fulladder_7_carryout));
  fullAdder fulladder_8 (.CarryIn(CIN), .A(X[0]), .B(Y[0]), .SumOut(SUM[0]), .CarryOut(fulladder_8_carryout));
endmodule

module customComparator (
  input  [7:0] X,
  input  [7:0] Y,
  output EQUAL
);

  wire xnor_1_out, xnor_2_out, xnor_3_out, xnor_4_out, xnor_5_out, xnor_6_out, xnor_7_out, xnor_8_out;

  xnor xnor_1 (xnor_1_out, X[0], Y[0]);
  xnor xnor_2 (xnor_2_out, X[1], Y[1]);
  xnor xnor_3 (xnor_3_out, X[2], Y[2]);
  xnor xnor_4 (xnor_4_out, X[3], Y[3]);
  xnor xnor_5 (xnor_5_out, X[4], Y[4]);
  xnor xnor_6 (xnor_6_out, X[5], Y[5]);
  xnor xnor_7 (xnor_7_out, X[6], Y[6]);
  xnor xnor_8 (xnor_8_out, X[7], Y[7]);
  and and_1 (EQUAL, xnor_1_out, xnor_2_out, xnor_3_out, xnor_4_out, xnor_5_out, xnor_6_out, xnor_7_out, xnor_8_out);
endmodule

module ALU8 (
  input  [7:0] X,
  input  [7:0] Y,
  input  [1:0] Opcode,
  output [7:0] RESULT,
  output EQ,
  output OVF,
  output CF,
  output ZF,
  output SF
);

  wire [7:0] AndOp, EightBitFAdder_sum, OrOp, RotateRight;

  customComparator customComp (.Y(Y), .X(X), .EQUAL(EQ));
  rotr u_RotateRight (.X(X), .Y(Y[2:0]), .ROUT(RotateRight));
  assign AndOp = X & Y;  // AND_Gate and_1, 8 bits wide
  assign OrOp = X | Y;  // OR_Gate or_1, 8 bits wide
  nor nor_1 (ZF, RESULT[0], RESULT[1], RESULT[2], RESULT[3], RESULT[4], RESULT[5], RESULT[6], RESULT[7]);
  Multiplexer #(.enable("true"), .select(2), .width(8)) multiplexer_1 (
    .in0(EightBitFAdder_sum), .in1(OrOp), .in2(AndOp), .in3(RotateRight), .out(RESULT), .sel(Opcode));  // open: en
  and and_2 (OVF, CF, RESULT[7]);
  FULLADDER8 EightBitFAdder (.Y(X), .X(Y), .COUT(CF), .SUM(EightBitFAdder_sum));  // open: CIN

  assign SF = RESULT[7];

  // Other names for the same wires on the sheet: Opc[1:0] = Opcode; SumOut[7:0] = RESULT
endmodule
