// Logisim project 8bitCPU_FIXED.circ as structural Verilog
module ControlUnit (
  input  [3:0] Opcode,
  input  EQ,
  output [1:0] Mux1,
  output Write,
  output Read,
  output Jal,
  output Mux2,
  output [1:0] PCmux,
  output [2:0] Ra_Reg,
  output WE,
  output Branch,
  output [2:0] AluFunc
);

  wire and_2_out, and_3_out, and_4_out, and_5_out, and_6_out, and_7_out, and_8_out, and_9_out, and_10_out,
       and_11_out, and_12_out, and_13_out, and_14_out, and_15_out, and_16_out, and_17_out, and_18_out,
       and_21_out, and_22_out, and_23_out, and_24_out, and_25_out, not_1_out, not_2_out, not_3_out,
       not_4_out, not_5_out, not_6_out, not_7_out, not_8_out, not_9_out, not_10_out, not_11_out, not_12_out,
       not_13_out, not_14_out, not_15_out, not_16_out, not_17_out, not_18_out, not_19_out, not_20_out,
       not_21_out, not_22_out, not_23_out, not_24_out, not_25_out, not_26_out, not_27_out, not_28_out,
       or_1_out;

  not not_1 (not_1_out, Opcode[0]);
  and and_1 (Jal, not_1_out, Opcode[1], Opcode[2], Opcode[3]);
  not not_2 (not_2_out, Opcode[1]);
  not not_3 (not_3_out, Opcode[3]);
  not not_4 (not_4_out, Opcode[2]);
  not not_5 (not_5_out, Opcode[2]);
  and and_2 (and_2_out, not_5_out, not_6_out);
  not not_6 (not_6_out, Opcode[3]);
  not not_7 (not_7_out, Opcode[0]);
  not not_8 (not_8_out, Opcode[1]);
  and and_3 (and_3_out, Opcode[2], Opcode[3]);
  not not_9 (not_9_out, or_1_out);
  or or_1 (or_1_out, Opcode[2], Opcode[3]);
  not not_10 (not_10_out, EQ);
  and and_4 (and_4_out, Opcode[1], Opcode[3]);
  and and_5 (and_5_out, Opcode[0], not_2_out, not_3_out);
  not not_11 (not_11_out, and_5_out);
  and and_6 (and_6_out, not_4_out, Opcode[1], Opcode[0]);
  and and_7 (and_7_out, and_2_out, Opcode[0]);
  and and_8 (and_8_out, and_2_out, Opcode[1]);
  and and_9 (and_9_out, not_7_out, not_8_out);
  and and_10 (and_10_out, Opcode[1], and_3_out);
  and and_11 (and_11_out, not_9_out, Opcode[0]);
  not not_12 (not_12_out, Opcode[1]);
  and and_12 (and_12_out, Opcode[0], not_12_out, Opcode[2], Opcode[3]);
  not not_13 (not_13_out, Opcode[2]);
  not not_14 (not_14_out, Opcode[0]);
  not not_15 (not_15_out, Opcode[1]);
  not not_16 (not_16_out, Opcode[3]);
  and and_13 (and_13_out, Opcode[2], not_17_out);
  not not_17 (not_17_out, Opcode[0]);
  and and_14 (and_14_out, and_4_out, and_13_out);
  or or_2 (Mux2, and_7_out, and_8_out);
  and and_15 (and_15_out, Opcode[0], Opcode[1], not_13_out, Opcode[3]);
  and and_16 (and_16_out, not_14_out, Opcode[1], Opcode[2], Opcode[3]);
  and and_17 (and_17_out, Opcode[2], not_15_out, Opcode[0], EQ);
  and and_18 (and_18_out, not_16_out, Opcode[2], Opcode[1], Opcode[0], not_10_out);
  or or_3 (Mux1[0], and_5_out, and_14_out);
  or or_4 (Mux1[1], and_14_out, and_6_out);
  or or_5 (WE, and_9_out, and_10_out, and_11_out);
  or or_6 (Branch, and_12_out, and_15_out, and_16_out, and_17_out, and_18_out);
  not not_18 (not_18_out, Opcode[2]);
  not not_19 (not_19_out, Opcode[3]);
  not not_20 (not_20_out, Opcode[0]);
  not not_21 (not_21_out, Opcode[1]);
  not not_22 (not_22_out, Opcode[3]);
  not not_23 (not_23_out, Opcode[1]);
  not not_24 (not_24_out, Opcode[0]);
  not not_25 (not_25_out, Opcode[1]);
  not not_26 (not_26_out, Opcode[2]);
  and and_19 (Write, not_20_out, Opcode[1], not_18_out, not_19_out);
  and and_20 (Read, not_19_out, not_18_out, Opcode[0], not_21_out);
  and and_21 (and_21_out, not_22_out, Opcode[2], Opcode[0]);
  and and_22 (and_22_out, Opcode[2], not_23_out, Opcode[0]);
  and and_23 (and_23_out, not_24_out, Opcode[1], Opcode[2], Opcode[3]);
  and and_24 (and_24_out, Opcode[0], not_25_out, Opcode[2], Opcode[3]);
  and and_25 (and_25_out, Opcode[0], Opcode[1], not_26_out, Opcode[3]);
  not not_27 (not_27_out, Opcode[1]);
  not not_28 (not_28_out, Opcode[0]);
  and and_26 (AluFunc[0], Opcode[2], not_27_out);
  and and_27 (AluFunc[1], not_27_out, Opcode[3], not_28_out);
  and and_28 (AluFunc[2], Opcode[2], Opcode[0]);
  or or_7 (PCmux[0], and_21_out, and_22_out);
  or or_8 (PCmux[1], and_23_out, and_24_out, and_25_out);

  assign Ra_Reg = 3'b111;

  // Other names for the same wires on the sheet: op0 = Opcode[0]; op1 = Opcode[1]; op2 = Opcode[2]; op3 = Opcode[3]
endmodule

// ALU
module ALU8 (
  input  [7:0] X,
  input  [7:0] Y,
  input  [2:0] ALUfunc,
  output [7:0] RESULT,
  output EQ
);

  wire comparator_1_lt;
  wire [7:0] adder_1_out, and_1_out, bit_extender_1_out, or_1_out, shifter_1_out;

  Comparator comparator_1 (.a(X), .b(Y), .eq(EQ), .lt(comparator_1_lt));  // open: gt
  Adder adder_1 (.a(X), .b(Y), .out(adder_1_out));  // open: cin, cout
  Shifter #(.shift("rl")) shifter_1 (.in(X), .\dist (Y[2:0]), .out(shifter_1_out));
  assign and_1_out = X & Y;  // AND_Gate and_1, 8 bits wide
  assign or_1_out = X | Y;  // OR_Gate or_1, 8 bits wide
  assign bit_extender_1_out = {{7{comparator_1_lt}}, comparator_1_lt};  // Bit_Extender bit_extender_1
  Multiplexer #(.select(3), .width(8)) multiplexer_1 (
    .in0(adder_1_out), .in1(and_1_out), .in2(or_1_out), .in3(shifter_1_out), .in4(bit_extender_1_out),
    .out(RESULT), .sel(ALUfunc));  // open: in5, in6, in7
endmodule

module RegisterFile (
  input  WE,
  input  [2:0] Rd,
  input  [7:0] Data,
  input  Clock,
  input  [2:0] Rt,
  input  [2:0] Rs,
  output [7:0] RtOut,
  output [7:0] RsOut
);

  wire decoder_1_out0, decoder_1_out1, decoder_1_out2, decoder_1_out3, decoder_1_out4, decoder_1_out5,
       decoder_1_out6, decoder_1_out7;
  wire [7:0] register_1_q, register_2_q, register_3_q, register_4_q, register_5_q, register_6_q,
       register_7_q, register_8_q;

  Decoder #(.select(3)) decoder_1 (
    .out0(decoder_1_out0), .out1(decoder_1_out1), .out2(decoder_1_out2), .out3(decoder_1_out3),
    .out4(decoder_1_out4), .out5(decoder_1_out5), .out6(decoder_1_out6), .out7(decoder_1_out7), .sel(Rd),
    .en(WE));
  Register #(.trigger("falling")) register_1 (
    .D(Data), .en(decoder_1_out0), .clk(Clock), .Q(register_1_q));  // open: clr
  Register #(.trigger("falling")) register_2 (
    .D(Data), .en(decoder_1_out1), .clk(Clock), .Q(register_2_q));  // open: clr
  Register #(.trigger("falling")) register_3 (
    .D(Data), .en(decoder_1_out2), .clk(Clock), .Q(register_3_q));  // open: clr
  Register #(.trigger("falling")) register_4 (
    .D(Data), .en(decoder_1_out3), .clk(Clock), .Q(register_4_q));  // open: clr
  Register #(.trigger("falling")) register_5 (
    .D(Data), .en(decoder_1_out4), .clk(Clock), .Q(register_5_q));  // open: clr
  Register #(.trigger("falling")) register_6 (
    .D(Data), .en(decoder_1_out5), .clk(Clock), .Q(register_6_q));  // open: clr
  Register #(.trigger("falling")) register_7 (
    .D(Data), .en(decoder_1_out6), .clk(Clock), .Q(register_7_q));  // open: clr
  Register #(.trigger("falling")) register_8 (
    .D(Data), .en(decoder_1_out7), .clk(Clock), .Q(register_8_q));  // open: clr
  Multiplexer #(.select(3), .width(8)) multiplexer_1 (
    .in0(register_1_q), .in1(register_2_q), .in2(register_3_q), .in3(register_4_q), .in4(register_5_q),
    .in5(register_6_q), .in6(register_7_q), .in7(register_8_q), .out(RtOut), .sel(Rt));
  Multiplexer #(.select(3), .width(8)) multiplexer_2 (
    .in0(register_1_q), .in1(register_2_q), .in2(register_3_q), .in3(register_4_q), .in4(register_5_q),
    .in5(register_6_q), .in6(register_7_q), .in7(register_8_q), .out(RsOut), .sel(Rs));
endmodule

module InstructionMemory (
  input  [9:0] PC,
  output [3:0] Opcode,
  output [2:0] Rs,
  output [2:0] Rt,
  output [2:0] Rd,
  output [7:0] I,
  output [9:0] JumpIMM
);

  ROM #(.addrWidth(10), .dataWidth(21), .misaligned("true")) ProgramROM (
    .addr(PC), .data({Opcode, Rs, Rt, Rd[2], JumpIMM[9:8], I}));

  assign JumpIMM[7:0] = I;
  assign Rd[1:0] = JumpIMM[9:8];

  // Notes on the sheet:
  //   contents of ProgramROM (hex, n*v repeats v):
  //   60307 60502 1c0009 1ee100 60403 e703 20201 bd006 18ec00 42001 1bc000 8d600 f5002 16000c 43004
endmodule

module ProgramCounter (
  input  [9:0] PC_IN,
  input  Clock,
  input  R,
  output [9:0] Counter
);

  Register #(.width(10)) register_1 (.D(PC_IN), .clk(Clock), .Q(Counter), .clr(R));  // open: en
endmodule

module CPU (
  input  Reset,
  output [9:0] PC_OUT,
  output [7:0] out_3
);

  wire Clk, controlunit_1_branch, controlunit_1_jal, controlunit_1_read, controlunit_1_we,
       controlunit_1_write, EQ, MUX2;
  wire [1:0] bit_extender_2_out, controlunit_1_pcmux, MUX1, Mux3;
  wire [2:0] controlunit_1_alufunc, controlunit_1_ra_reg, instructionmemory_1_rd, instructionmemory_1_rs,
       instructionmemory_1_rt, multiplexer_3_out;
  wire [3:0] instructionmemory_1_opcode;
  wire [7:0] bit_extender_1_out, Immediate, multiplexer_2_out, multiplexer_4_out, registerfile_1_rtout,
       Result, RS;
  wire [9:0] bit_extender_3_out, BranchIMM_ex, JumpIMM, multiplexer_1_out, Ra_Addr;

  Clock clock_1 (.out(Clk));
  Multiplexer #(.select(2), .width(10)) multiplexer_1 (
    .in0(Ra_Addr), .in1(BranchIMM_ex), .in2(JumpIMM), .in3(bit_extender_3_out), .out(multiplexer_1_out),
    .sel(Mux3));
  Adder #(.width(10)) adder_1 (.a(PC_OUT), .b(10'h1), .out(Ra_Addr));  // open: cin, cout
  ProgramCounter programcounter_1 (.PC_IN(multiplexer_1_out), .Clock(Clk), .R(Reset), .Counter(PC_OUT));
  assign Mux3 = bit_extender_2_out & controlunit_1_pcmux;  // AND_Gate and_1, 2 bits wide
  Bit_Extender #(.in_width(10), .out_width(8)) bit_extender_1 (.in(Ra_Addr), .out(bit_extender_1_out));
  assign bit_extender_2_out = {{1{1'b1}}, controlunit_1_branch};  // Bit_Extender bit_extender_2
  assign bit_extender_3_out = {{2{RS[7]}}, RS};  // Bit_Extender bit_extender_3
  InstructionMemory instructionmemory_1 (
    .PC(PC_OUT), .Opcode(instructionmemory_1_opcode), .Rs(instructionmemory_1_rs),
    .Rt(instructionmemory_1_rt), .Rd(instructionmemory_1_rd), .I(Immediate), .JumpIMM(JumpIMM));
  assign BranchIMM_ex = {{2{Immediate[7]}}, Immediate};  // Bit_Extender bit_extender_4
  Multiplexer #(.select(2), .width(8)) multiplexer_2 (
    .in0(Result), .in1(out_3), .in2(Immediate), .in3(bit_extender_1_out), .out(multiplexer_2_out), .sel(MUX1));
  ControlUnit controlunit_1 (
    .Opcode(instructionmemory_1_opcode), .EQ(EQ), .Mux1(MUX1), .Write(controlunit_1_write),
    .Read(controlunit_1_read), .Jal(controlunit_1_jal), .Mux2(MUX2), .PCmux(controlunit_1_pcmux),
    .Ra_Reg(controlunit_1_ra_reg), .WE(controlunit_1_we), .Branch(controlunit_1_branch),
    .AluFunc(controlunit_1_alufunc));
  Multiplexer #(.width(3)) multiplexer_3 (
    .in0(instructionmemory_1_rd), .in1(controlunit_1_ra_reg), .out(multiplexer_3_out), .sel(controlunit_1_jal));
  RegisterFile registerfile_1 (
    .WE(controlunit_1_we), .Rd(multiplexer_3_out), .Data(multiplexer_2_out), .Clock(Clk),
    .Rt(instructionmemory_1_rt), .Rs(instructionmemory_1_rs), .RtOut(registerfile_1_rtout), .RsOut(RS));
  RAM #(.asyncread("true")) ProgramRAM (
    .addr(Result), .we(controlunit_1_write), .oe(controlunit_1_read), .clk(Clk), .din(registerfile_1_rtout),
    .dout(out_3));
  Multiplexer #(.width(8)) multiplexer_4 (
    .in0(registerfile_1_rtout), .in1(Immediate), .out(multiplexer_4_out), .sel(MUX2));
  ALU8 alu8_1 (.X(RS), .Y(multiplexer_4_out), .ALUfunc(controlunit_1_alufunc), .RESULT(Result), .EQ(EQ));

  // Other names for the same wires on the sheet: RamOut[7:0] = out_3
endmodule
