// Logisim project Processor-Core.circ as structural Verilog
// ALU
module ALU8 (
  input  [7:0] X,
  input  [7:0] Y,
  input  [1:0] ALUfunc,
  output [7:0] RESULT
);

  wire [7:0] adder_1_out, and_1_out, or_1_out, shifter_1_out;

  Adder adder_1 (.a(X), .b(Y), .out(adder_1_out));  // open: cin, cout
  Shifter #(.shift("rl")) shifter_1 (.in(X), .\dist (Y[2:0]), .out(shifter_1_out));
  assign and_1_out = X & Y;  // AND_Gate and_1, 8 bits wide
  assign or_1_out = X | Y;  // OR_Gate or_1, 8 bits wide
  Multiplexer #(.select(2), .width(8)) multiplexer_1 (
    .in0(adder_1_out), .in1(and_1_out), .in2(or_1_out), .in3(shifter_1_out), .out(RESULT), .sel(ALUfunc));
endmodule

module ControlUnit (
  input  [3:0] Opcode,
  output [1:0] MUX1,
  output [1:0] AluFunc,
  output MUX2,
  output WE,
  output Write,
  output Read
);

  wire not_1_out, not_2_out, not_3_out, not_4_out;

  not not_1 (not_1_out, Opcode[1]);
  not not_2 (not_2_out, Opcode[1]);
  not not_3 (not_3_out, Opcode[0]);
  not not_4 (not_4_out, Opcode[1]);
  and and_1 (MUX1[1], Opcode[0], Opcode[1]);
  and and_2 (MUX1[0], not_1_out, Opcode[0]);
  or or_1 (MUX2, Opcode[1], Opcode[0]);
  or or_2 (WE, not_2_out, Opcode[0]);
  and and_3 (Write, Opcode[1], not_3_out);
  and and_4 (Read, not_4_out, Opcode[0]);

  assign AluFunc = Opcode[3:2];
endmodule

module RegisterFile (
  input  WE,
  input  [2:0] Rd,
  input  [7:0] Data,
  input  Clock,
  input  [2:0] Rt,
  input  [2:0] Rs,
  output [7:0] RtOut,
  output [7:0] RsOut
);

  wire decoder_1_out0, decoder_1_out1, decoder_1_out2, decoder_1_out3, decoder_1_out4, decoder_1_out5,
       decoder_1_out6, decoder_1_out7;
  wire [7:0] register_1_q, register_2_q, register_3_q, register_4_q, register_5_q, register_6_q,
       register_7_q, register_8_q;

  Decoder #(.select(3)) decoder_1 (
    .out0(decoder_1_out0), .out1(decoder_1_out1), .out2(decoder_1_out2), .out3(decoder_1_out3),
    .out4(decoder_1_out4), .out5(decoder_1_out5), .out6(decoder_1_out6), .out7(decoder_1_out7), .sel(Rd),
    .en(WE));
  Register #(.trigger("falling")) register_1 (
    .D(Data), .en(decoder_1_out0), .clk(Clock), .Q(register_1_q));  // open: clr
  Register #(.trigger("falling")) register_2 (
    .D(Data), .en(decoder_1_out1), .clk(Clock), .Q(register_2_q));  // open: clr
  Register #(.trigger("falling")) register_3 (
    .D(Data), .en(decoder_1_out2), .clk(Clock), .Q(register_3_q));  // open: clr
  Register #(.trigger("falling")) register_4 (
    .D(Data), .en(decoder_1_out3), .clk(Clock), .Q(register_4_q));  // open: clr
  Register #(.trigger("falling")) register_5 (
    .D(Data), .en(decoder_1_out4), .clk(Clock), .Q(register_5_q));  // open: clr
  Register #(.trigger("falling")) register_6 (
    .D(Data), .en(decoder_1_out5), .clk(Clock), .Q(register_6_q));  // open: clr
  Register #(.trigger("falling")) register_7 (
    .D(Data), .en(decoder_1_out6), .clk(Clock), .Q(register_7_q));  // open: clr
  Register #(.trigger("falling")) register_8 (
    .D(Data), .en(decoder_1_out7), .clk(Clock), .Q(register_8_q));  // open: clr
  Multiplexer #(.select(3), .width(8)) multiplexer_1 (
    .in0(register_1_q), .in1(register_2_q), .in2(register_3_q), .in3(register_4_q), .in4(register_5_q),
    .in5(register_6_q), .in6(register_7_q), .in7(register_8_q), .out(RtOut), .sel(Rt));
  Multiplexer #(.select(3), .width(8)) multiplexer_2 (
    .in0(register_1_q), .in1(register_2_q), .in2(register_3_q), .in3(register_4_q), .in4(register_5_q),
    .in5(register_6_q), .in6(register_7_q), .in7(register_8_q), .out(RsOut), .sel(Rs));
endmodule

module InstructionMemory (
  input  [9:0] PC,
  output [3:0] Opcode,
  output [2:0] Rs,
  output [2:0] Rt,
  output [2:0] Rd,
  output [7:0] I
);

  ROM #(.addrWidth(10), .dataWidth(21), .misaligned("true")) ProgramROM (.addr(PC), .data({Opcode, Rs, Rt, Rd, I}));

  // Notes on the sheet:
  //   contents of ProgramROM (hex, n*v repeats v):
  //   60503 60702 1ee00 197c00 43002 9a200 20302 10e602 15100 40805
endmodule

module ProgramCounter (
  input  [9:0] PC_IN,
  input  Clock,
  input  R,
  output [9:0] Counter
);

  Register #(.width(10)) register_1 (.D(PC_IN), .clk(Clock), .Q(Counter), .clr(R));  // open: en
endmodule

module CPU (
  input  Reset,
  output [9:0] PC_OUT,
  output [7:0] out_3
);

  wire Clock, controlunit_1_read, controlunit_1_we, controlunit_1_write, MUX2;
  wire [1:0] controlunit_1_alufunc, MUX1;
  wire [2:0] instructionmemory_1_rd, instructionmemory_1_rs, instructionmemory_1_rt;
  wire [3:0] instructionmemory_1_opcode;
  wire [7:0] Immediate, multiplexer_1_out, multiplexer_2_out, registerfile_1_rsout, registerfile_1_rtout,
       Result;
  wire [9:0] adder_1_out;

  Clock clock_1 (.out(Clock));
  Adder #(.width(10)) adder_1 (.a(PC_OUT), .b(10'h1), .out(adder_1_out));  // open: cin, cout
  ProgramCounter programcounter_1 (.PC_IN(adder_1_out), .Clock(Clock), .R(Reset), .Counter(PC_OUT));
  InstructionMemory instructionmemory_1 (
    .PC(PC_OUT), .Opcode(instructionmemory_1_opcode), .Rs(instructionmemory_1_rs),
    .Rt(instructionmemory_1_rt), .Rd(instructionmemory_1_rd), .I(Immediate));
  Multiplexer #(.select(2), .width(8)) multiplexer_1 (
    .in0(Result), .in1(out_3), .in2(Immediate), .out(multiplexer_1_out), .sel(MUX1));  // open: in3
  ControlUnit controlunit_1 (
    .Opcode(instructionmemory_1_opcode), .MUX1(MUX1), .AluFunc(controlunit_1_alufunc), .MUX2(MUX2),
    .WE(controlunit_1_we), .Write(controlunit_1_write), .Read(controlunit_1_read));
  RegisterFile registerfile_1 (
    .WE(controlunit_1_we), .Rd(instructionmemory_1_rd), .Data(multiplexer_1_out), .Clock(Clock),
    .Rt(instructionmemory_1_rt), .Rs(instructionmemory_1_rs), .RtOut(registerfile_1_rtout),
    .RsOut(registerfile_1_rsout));
  Multiplexer #(.width(8)) multiplexer_2 (
    .in0(registerfile_1_rtout), .in1(Immediate), .out(multiplexer_2_out), .sel(MUX2));
  ALU8 alu8_1 (.X(registerfile_1_rsout), .Y(multiplexer_2_out), .ALUfunc(controlunit_1_alufunc), .RESULT(Result));
  RAM #(.asyncread("true")) ProgramRAM (
    .addr(Result), .we(controlunit_1_write), .oe(controlunit_1_read), .clk(Clock),
    .din(registerfile_1_rtout), .dout(out_3));

  // Other names for the same wires on the sheet: RamOut[7:0] = out_3
endmodule
